# Fritzing sketch schematics (saved by Fritzing 1.0.4)
breadboards: 1

parts:
  A1 = ESP32 DevKitc V4
  M1 = MAX7219 8x8 single Led Matrix Module

nets:
  N1: A1.Pin_14, A1.Pin_32, A1.Pin_38, M1.I-GND-1, M1.O-GND-1, M1.I-GND-2, M1.O-GND-2, M1.I-GND-3, M1.O-GND-3, M1.I-GND-4
  N2: A1.Pin_19, M1.I-VCC-1, M1.O-VCC-1, M1.I-VCC-2, M1.O-VCC-2, M1.I-VCC-3, M1.O-VCC-3, M1.I-VCC-4
  N3: A1.Pin_29, M1.I-CLK-1, M1.O-CLK-1, M1.I-CLK-2, M1.O-CLK-2, M1.I-CLK-3, M1.O-CLK-3, M1.I-CLK-4
  N4: A1.Pin_33, M1.I-CS-1, M1.O-CS-1, M1.I-CS-2, M1.O-CS-2, M1.I-CS-3, M1.O-CS-3, M1.I-CS-4
  N5: A1.Pin_37, M1.I-DIN-1
  N6: M1.O-DOUT-1, M1.I-DIN-2
  N7: M1.O-DOUT-2, M1.I-DIN-3
  N8: M1.O-DOUT-3, M1.I-DIN-4

custom parts:
  ESP32 DevKitc V4: ESP32-DevKitC board with ESP32-WROOM-32 module. ESP32-DevKitC V4 is a small-sized ESP32-based development board produced by Espressif. Most of the pins on the ESP module are broken out to the pin headers on the board. The pins D0, D1, D2, D3, CMD and CLK are used internally for communication between ESP32 and SPI flash memory. They are grouped on both sides near the USB connector. Avoid using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
  MAX7219 8x8 single Led Matrix Module: Description: MAX7219 8x8 LedMatrix single Red Module Dimensions: 32x32mm Documents:
